# Fritzing sketch BareMetalArduino (saved by Fritzing 0.9.2b)
breadboards: 1

parts:
  C1 = Ceramic Capacitor [capacitance=100nF package="100 mil [THT, multilayer]"]
  R1 = Resistor [tolerance=±5% resistance=10k package=THT]
  LED1 = LED - 5mm [color="Red (633nm)" package="5 mm [THT]"]
  R2 = Resistor [tolerance=±5% resistance=220 package=THT]
  S1 = Pushbutton [package="[THT]"]
  U1 = atmega168 [package=dip]
  R3 = Resistor [tolerance=±5% resistance=10k package=THT]

nets:
  GND: C1.0, LED1.cathode, S1.Pin_3, S1.Pin_4, U1.GND
  5V: C1.1, R1.Pin_0, U1.VCC, U1.AVCC, U1.AREF, R3.Pin_0
  N1: R1.Pin_1, U1.RESET
  N2: LED1.anode, R2.Pin_1
  N3: R2.Pin_0, U1.D13
  N4: S1.Pin_1, U1.D2, R3.Pin_1

notes:
  Baremetal Arduino, "Arduino" on breadboard as part of the Arduino Unleashed coarse., 1.0
  http://interactionstation.wdka.hro.nl/wiki/Baremetal_arduino
